# Fritzing sketch Automatic Fish Feeder (saved by Fritzing 0.9.3b)
breadboards: 1

parts:
  R1 = Resistor [tolerance=±5% resistance=1k package=THT]
  Q1 = Basic FET N-Channel [package="TO220 [THT]"]
  M1 = DC Motor
  Part1 = Arduino Uno (Rev3)
  R2 = Resistor [tolerance=±5% resistance=220 package=THT]
  LED1 = LED - 5mm [color="Red (633nm)" package="5 mm [THT]"]

nets:
  N1: R1.Pin_0, Part1.D13/SCK
  N2: R1.Pin_1, Q1.gate
  N3: Q1.drain, M1.pin_1
  N4: Q1.source, Part1.GND, LED1.anode
  N5: M1.pin_2, Part1.5V
  N6: Part1.D7, R2.Pin_0
  N7: R2.Pin_1, LED1.cathode

notes:
  power the arduino using an AC power source connected via the serial cable. (I used an old mobile charger adapter to the USB-Serial cord of arduino)
  added a fan to DC motor .and kept it insde a case with 2 small holes. When the fan runs the fish food inside gets thrown out of the case via those holes into my fish tank.
